# Fritzing sketch wiring (saved by Fritzing 0.9.3b)

parts:
  U1 = NodeMCU V1.0
  元件1 = BME280 Breakout
  Part1 = Adafruit SGP30 Gas Sensor

nets:
  3V3: U1.3V3, 元件1.3.3V, Part1.VIN
  GND: U1.GND, 元件1.GND, Part1.GND
  N1: U1.D5, 元件1.SCK/SCL, Part1.SCL
  N2: U1.D6, 元件1.SDI/SDA, Part1.SDA

custom parts:
  NodeMCU V1.0: ESP8266 based NodeMCU
