# Fritzing sketch wiring (saved by Fritzing 0.9.3b)

parts:
  U1 = NodeMCU V1.0
  元件1 = BME280 Breakout

nets:
  3V3: U1.3V3, 元件1.3.3V
  GND: U1.GND, 元件1.GND
  N1: U1.D5, 元件1.SCK/SCL
  N2: U1.D6, 元件1.SDI/SDA

custom parts:
  NodeMCU V1.0: ESP8266 based NodeMCU
