# Fritzing sketch US-100_Webserver_wiring (saved by Fritzing 0.9.3b)

parts:
  U1 = NodeMCU V1.0
  hc-sr1 = hc-sr04

nets:
  N1: U1.D7, hc-sr1.Trig
  N2: U1.D8, hc-sr1.Echo
  GND: U1.GND, hc-sr1.GND
  3V3: U1.3V3, hc-sr1.VCC

custom parts:
  NodeMCU V1.0: ESP8266 based NodeMCU
