# Fritzing sketch flamesensor_Webserver_wiring (saved by Fritzing 0.9.3b)

parts:
  S1 = KY-026
  U2 = NodeMCU V1.0

nets:
  N1: S1.pin2, U2.GND
  N2: S1.pin3, U2.3V3
  N3: S1.pin4, U2.D5

custom parts:
  KY-026: ky-026 flame sensor module
  NodeMCU V1.0: ESP8266 based NodeMCU
