# Fritzing sketch vl53l0x_Webserver_wiring (saved by Fritzing 0.9.3b)

parts:
  U1 = NodeMCU V1.0
  Part1 = Adafruit VL53L0X Time of Flight Distance Sensor [part_number="Adafruit #3317"]

nets:
  3V3: U1.3V3, Part1.VIN
  GND: U1.GND, Part1.GND
  N1: U1.D5, Part1.SCL
  N2: U1.D6, Part1.SDA

custom parts:
  NodeMCU V1.0: ESP8266 based NodeMCU
  Adafruit VL53L0X Time of Flight Distance Sensor: The VL53L0X is a Time of Flight distance sensor like no other you've used! The sensor contains a very tiny invisible laser source, and a matching sensor. The VL53L0X can detect the "time of flight", or how long the light has taken to bounce back to the sensor. Since it uses a very narrow light source, it is good for determining distance of only the surface directly in front of it. Unlike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
