# Fritzing sketch vl53l0x_oled (saved by Fritzing 0.9.3b)
breadboards: 1

parts:
  Squix1 = OLED 0.96" 128x64 I2C SSD1306
  Part1 = Adafruit VL53L0X Time of Flight Distance Sensor [part_number="Adafruit #3317"]
  U1 = NodeMCU V1.0

nets:
  VCC: Squix1.VCC, Part1.VIN, U1.3V3
  GND: Squix1.GND, Part1.GND, U1.GND
  N1: Squix1.SCL, Part1.SCL, U1.D2
  N2: Squix1.SCA, Part1.SDA, U1.D1

custom parts:
  Adafruit VL53L0X Time of Flight Distance Sensor: The VL53L0X is a Time of Flight distance sensor like no other you've used! The sensor contains a very tiny invisible laser source, and a matching sensor. The VL53L0X can detect the "time of flight", or how long the light has taken to bounce back to the sensor. Since it uses a very narrow light source, it is good for determining distance of only the surface directly in front of it. Unlike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
  NodeMCU V1.0: ESP8266 based NodeMCU
